// Logisim project tictactoe.circ as structural Verilog: 5 circuits, main circuit main
module main (
  output out_1
);

  wire button_1_out, button_2_out, button_3_out, button_4_out, button_5_out, button_6_out, button_7_out,
       button_8_out, button_9_out, button_10_out, button_11_out, button_12_out, button_13_out, button_14_out,
       button_15_out, button_16_out, button_17_out, button_18_out, controlled_buffer_1_out, not_1_out,
       subcir_1_out_20;
  wire [2:0] subcir_1_out_21, subcir_1_out_22, subcir_1_out_23, subcir_1_out_24, subcir_1_out_25,
       subcir_1_out_26, subcir_1_out_27, subcir_1_out_28, subcir_1_out_29, subcir_1_out_30, subcir_1_out_31,
       subcir_1_out_32, subcir_1_out_33, subcir_1_out_34, subcir_1_out_35, subcir_1_out_37, subcir_1_out_38,
       subcir_1_out_39, subcir_1_out_40, subcir_1_out_41, subcir_1_out_42, subcir_1_out_43, subcir_1_out_44,
       subcir_1_out_45, subcir_1_out_46, subcir_1_out_47, subcir_1_out_48, subcir_1_out_49, subcir_1_out_50,
       subcir_1_out_51;

  Button button_1 (.out(button_1_out));
  Button button_2 (.out(button_2_out));
  Button button_3 (.out(button_3_out));
  Button button_4 (.out(button_4_out));
  Button button_5 (.out(button_5_out));
  Button button_6 (.out(button_6_out));
  Button button_7 (.out(button_7_out));
  Button button_8 (.out(button_8_out));
  Button button_9 (.out(button_9_out));
  Button button_10 (.out(button_10_out));
  Button button_11 (.out(button_11_out));
  Button button_12 (.out(button_12_out));
  Button button_13 (.out(button_13_out));
  Button button_14 (.out(button_14_out));
  Button button_15 (.out(button_15_out));
  Button button_16 (.out(button_16_out));
  Button button_17 (.out(button_17_out));
  Button button_18 (.out(button_18_out));
  assign controlled_buffer_1_out = not_1_out ? 1'b1 : 1'bz;  // Controlled_Buffer controlled_buffer_1
  not not_1 (not_1_out, subcir_1_out_20);
  DotMatrix #(.matrixcols(3), .matrixrows(3)) dotmatrix_1 (
    .col0(subcir_1_out_21), .col1(subcir_1_out_22), .col2(subcir_1_out_23));
  subcir subcir_1 (
    .in_2(button_1_out), .in_3(button_4_out), .in_4(button_7_out), .in_5(button_13_out), .in_6(button_8_out),
    .in_7(button_14_out), .in_8(button_2_out), .in_9(button_5_out), .in_10(button_9_out),
    .in_11(button_16_out), .in_12(button_10_out), .in_13(button_15_out), .in_14(button_3_out),
    .in_15(button_6_out), .in_16(button_11_out), .in_17(button_18_out), .in_18(button_12_out),
    .in_19(button_17_out), .in_1(controlled_buffer_1_out), .out_20(subcir_1_out_20),
    .out_21(subcir_1_out_21), .out_22(subcir_1_out_22), .out_23(subcir_1_out_23), .out_36(out_1),
    .out_24(subcir_1_out_24), .out_25(subcir_1_out_25), .out_26(subcir_1_out_26), .out_27(subcir_1_out_27),
    .out_28(subcir_1_out_28), .out_29(subcir_1_out_29), .out_30(subcir_1_out_30), .out_31(subcir_1_out_31),
    .out_32(subcir_1_out_32), .out_33(subcir_1_out_33), .out_34(subcir_1_out_34), .out_35(subcir_1_out_35),
    .out_37(subcir_1_out_37), .out_38(subcir_1_out_38), .out_39(subcir_1_out_39), .out_40(subcir_1_out_40),
    .out_41(subcir_1_out_41), .out_42(subcir_1_out_42), .out_43(subcir_1_out_43), .out_44(subcir_1_out_44),
    .out_45(subcir_1_out_45), .out_46(subcir_1_out_46), .out_47(subcir_1_out_47), .out_48(subcir_1_out_48),
    .out_49(subcir_1_out_49), .out_50(subcir_1_out_50), .out_51(subcir_1_out_51));
  DotMatrix #(.matrixcols(3), .matrixrows(3)) dotmatrix_2 (
    .col0(subcir_1_out_24), .col1(subcir_1_out_25), .col2(subcir_1_out_26));
  DotMatrix #(.matrixcols(3), .matrixrows(3)) dotmatrix_3 (
    .col0(subcir_1_out_27), .col1(subcir_1_out_28), .col2(subcir_1_out_29));
  DotMatrix #(.matrixcols(3), .matrixrows(3)) dotmatrix_4 (
    .col0(subcir_1_out_33), .col1(subcir_1_out_34), .col2(subcir_1_out_35));
  DotMatrix #(.matrixcols(3), .matrixrows(3)) dotmatrix_5 (
    .col0(subcir_1_out_37), .col1(subcir_1_out_38), .col2(subcir_1_out_39));
  DotMatrix #(.matrixcols(3), .matrixrows(3)) dotmatrix_6 (
    .col0(subcir_1_out_43), .col1(subcir_1_out_44), .col2(subcir_1_out_45));
  DotMatrix #(.matrixcols(3), .matrixrows(3)) dotmatrix_7 (
    .col0(subcir_1_out_46), .col1(subcir_1_out_47), .col2(subcir_1_out_48));
  DotMatrix #(.matrixcols(3), .matrixrows(3)) dotmatrix_8 (
    .col0(subcir_1_out_30), .col1(subcir_1_out_31), .col2(subcir_1_out_32));
  DotMatrix #(.matrixcols(3), .matrixrows(3)) dotmatrix_9 (
    .col0(subcir_1_out_40), .col1(subcir_1_out_41), .col2(subcir_1_out_42));
  DotMatrix #(.matrixcols(3), .matrixrows(3)) dotmatrix_10 (
    .col0(subcir_1_out_49), .col1(subcir_1_out_50), .col2(subcir_1_out_51));
endmodule

module subcir (
  input  in_1,
  input  in_2,
  input  in_3,
  input  in_4,
  input  in_5,
  input  in_6,
  input  in_7,
  input  in_8,
  input  in_9,
  input  in_10,
  input  in_11,
  input  in_12,
  input  in_13,
  input  in_14,
  input  in_15,
  input  in_16,
  input  in_17,
  input  in_18,
  input  in_19,
  output out_20,
  output [2:0] out_21,
  output [2:0] out_22,
  output [2:0] out_23,
  output [2:0] out_24,
  output [2:0] out_25,
  output [2:0] out_26,
  output [2:0] out_27,
  output [2:0] out_28,
  output [2:0] out_29,
  output [2:0] out_30,
  output [2:0] out_31,
  output [2:0] out_32,
  output [2:0] out_33,
  output [2:0] out_34,
  output [2:0] out_35,
  output out_36,
  output [2:0] out_37,
  output [2:0] out_38,
  output [2:0] out_39,
  output [2:0] out_40,
  output [2:0] out_41,
  output [2:0] out_42,
  output [2:0] out_43,
  output [2:0] out_44,
  output [2:0] out_45,
  output [2:0] out_46,
  output [2:0] out_47,
  output [2:0] out_48,
  output [2:0] out_49,
  output [2:0] out_50,
  output [2:0] out_51
);

  wire check_1_out_2, check_1_out_3, check_2_out_2, check_2_out_3, check_3_out_2, check_3_out_3,
       check_4_out_2, check_4_out_3, check_5_out_2, check_5_out_3, check_6_out_2, check_6_out_3,
       check_7_out_2, check_7_out_3, check_8_out_2, check_8_out_3, check_9_out_2, check_9_out_3, or_1_out,
       subsubcir_1_out_6, subsubcir_2_out_6, subsubcir_3_out_6, subsubcir_4_out_6, subsubcir_5_out_6,
       subsubcir_6_out_6, subsubcir_7_out_6, subsubcir_8_out_6, subsubcir_9_out_6, t_ff_1_qn;

  T_Flip_Flop t_ff_1 (.clk(or_1_out), .T(1'b1), .Q(out_36), .Qn(t_ff_1_qn), .en(1'b1));  // open: preset, reset
  subsubcir subsubcir_1 (
    .in_2(in_2), .in_3(in_3), .in_1(in_1), .out_6(subsubcir_1_out_6), .in_4(t_ff_1_qn), .in_5(out_36),
    .out_7(out_24), .out_8(out_25), .out_9(out_26));
  subsubcir subsubcir_2 (
    .in_2(in_4), .in_3(in_5), .in_1(in_1), .out_6(subsubcir_2_out_6), .in_4(t_ff_1_qn), .in_5(out_36),
    .out_7(out_27), .out_8(out_28), .out_9(out_29));
  subsubcir subsubcir_3 (
    .in_2(in_6), .in_3(in_7), .in_1(in_1), .out_6(subsubcir_3_out_6), .in_4(t_ff_1_qn), .in_5(out_36),
    .out_7(out_30), .out_8(out_31), .out_9(out_32));
  subsubcir subsubcir_4 (
    .in_2(in_8), .in_3(in_9), .in_1(in_1), .out_6(subsubcir_4_out_6), .in_4(t_ff_1_qn), .in_5(out_36),
    .out_7(out_33), .out_8(out_34), .out_9(out_35));
  subsubcir subsubcir_5 (
    .in_2(in_10), .in_3(in_11), .in_1(in_1), .out_6(subsubcir_5_out_6), .in_4(t_ff_1_qn), .in_5(out_36),
    .out_7(out_37), .out_8(out_38), .out_9(out_39));
  subsubcir subsubcir_6 (
    .in_2(in_12), .in_3(in_13), .in_1(in_1), .out_6(subsubcir_6_out_6), .in_4(t_ff_1_qn), .in_5(out_36),
    .out_7(out_40), .out_8(out_41), .out_9(out_42));
  subsubcir subsubcir_7 (
    .in_2(in_14), .in_3(in_15), .in_1(in_1), .out_6(subsubcir_7_out_6), .in_4(t_ff_1_qn), .in_5(out_36),
    .out_7(out_43), .out_8(out_44), .out_9(out_45));
  subsubcir subsubcir_8 (
    .in_2(in_16), .in_3(in_17), .in_1(in_1), .out_6(subsubcir_8_out_6), .in_4(t_ff_1_qn), .in_5(out_36),
    .out_7(out_46), .out_8(out_47), .out_9(out_48));
  subsubcir subsubcir_9 (
    .in_2(in_18), .in_3(in_19), .in_1(in_1), .out_6(subsubcir_9_out_6), .in_4(t_ff_1_qn), .in_5(out_36),
    .out_7(out_49), .out_8(out_50), .out_9(out_51));
  or or_1 (or_1_out, subsubcir_1_out_6, subsubcir_2_out_6, subsubcir_3_out_6, subsubcir_4_out_6, subsubcir_5_out_6, subsubcir_6_out_6, subsubcir_7_out_6, subsubcir_8_out_6, subsubcir_9_out_6);
  check check_1 (.in_1(out_24), .out_2(check_1_out_2), .out_3(check_1_out_3));
  check check_2 (.in_1(out_27), .out_2(check_2_out_2), .out_3(check_2_out_3));
  check check_3 (.in_1(out_30), .out_2(check_3_out_2), .out_3(check_3_out_3));
  check check_4 (.in_1(out_33), .out_2(check_4_out_2), .out_3(check_4_out_3));
  check check_5 (.in_1(out_37), .out_2(check_5_out_2), .out_3(check_5_out_3));
  check check_6 (.in_1(out_40), .out_2(check_6_out_2), .out_3(check_6_out_3));
  check check_7 (.in_1(out_43), .out_2(check_7_out_2), .out_3(check_7_out_3));
  check check_8 (.in_1(out_46), .out_2(check_8_out_2), .out_3(check_8_out_3));
  check check_9 (.in_1(out_49), .out_2(check_9_out_2), .out_3(check_9_out_3));
  who who_1 (
    .in_1(check_1_out_2), .in_2(check_2_out_2), .in_3(check_3_out_2), .in_4(check_4_out_2),
    .in_5(check_5_out_2), .in_6(check_6_out_2), .in_7(check_7_out_2), .in_8(check_8_out_2),
    .in_9(check_9_out_2), .in_10(check_1_out_3), .in_11(check_2_out_3), .in_12(check_3_out_3),
    .in_13(check_4_out_3), .in_14(check_5_out_3), .in_15(check_6_out_3), .in_16(check_7_out_3),
    .in_17(check_8_out_3), .in_18(check_9_out_3), .out_19(out_20), .out_20(out_21), .out_21(out_22),
    .out_22(out_23));
endmodule

module subsubcir (
  input  in_1,
  input  in_2,
  input  in_3,
  input  in_4,
  input  in_5,
  output out_6,
  output [2:0] out_7,
  output [2:0] out_8,
  output [2:0] out_9
);

  wire and_1_out, and_2_out, and_3_out, and_4_out, clock_1_out, d_ff_1_qn, d_ff_2_qn, d_ff_3_qn, or_2_out;

  or or_1 (out_6, and_2_out, and_1_out);
  and and_1 (and_1_out, d_ff_3_qn, out_7[1], in_3);
  and and_2 (and_2_out, d_ff_3_qn, out_8[1], in_2);
  and and_3 (and_3_out, d_ff_2_qn, in_2);
  and and_4 (and_4_out, in_3, d_ff_1_qn);
  D_Flip_Flop d_ff_1 (.clk(and_3_out), .D(in_1), .Q(out_8[1]), .Qn(d_ff_1_qn), .en(in_4));  // open: preset, reset
  D_Flip_Flop d_ff_2 (.clk(and_4_out), .D(in_1), .Q(out_7[1]), .Qn(d_ff_2_qn), .en(in_5));  // open: preset, reset
  Clock clock_1 (.out(clock_1_out));
  or or_2 (or_2_out, out_8[1], out_7[1]);
  D_Flip_Flop d_ff_3 (.clk(clock_1_out), .D(or_2_out), .Qn(d_ff_3_qn));  // open: Q, preset, en, reset
  or or_3 (out_7[2], out_7[1], out_8[1]);

  assign out_7[0] = out_7[2];
  assign {out_8[2], out_8[0]} = {2{out_7[1]}};
  assign out_9 = {out_7[2:1], out_7[2]};
endmodule

module who (
  input  in_1,
  input  in_2,
  input  in_3,
  input  in_4,
  input  in_5,
  input  in_6,
  input  in_7,
  input  in_8,
  input  in_9,
  input  in_10,
  input  in_11,
  input  in_12,
  input  in_13,
  input  in_14,
  input  in_15,
  input  in_16,
  input  in_17,
  input  in_18,
  output out_19,
  output [2:0] out_20,
  output [2:0] out_21,
  output [2:0] out_22
);

  wire and_1_out, and_2_out, and_3_out, and_4_out, and_5_out, and_6_out, and_7_out, and_8_out, and_9_out,
       and_10_out, and_11_out, and_12_out, and_13_out, and_14_out, and_15_out, and_16_out;

  and and_1 (and_1_out, in_1, in_2, in_3);
  and and_2 (and_2_out, in_18, in_17, in_16);
  and and_3 (and_3_out, in_4, in_5, in_6);
  and and_4 (and_4_out, in_15, in_14, in_13);
  and and_5 (and_5_out, in_7, in_8, in_9);
  and and_6 (and_6_out, in_3, in_6, in_9);
  and and_7 (and_7_out, in_12, in_11, in_10);
  or or_1 (out_21[1], and_1_out, and_3_out, and_5_out, and_6_out, and_8_out, and_11_out, and_13_out, and_14_out);
  and and_8 (and_8_out, in_2, in_5, in_8);
  and and_9 (and_9_out, in_16, in_13, in_10);
  and and_10 (and_10_out, in_17, in_14, in_11);
  or or_2 (out_20[1], and_2_out, and_4_out, and_7_out, and_9_out, and_10_out, and_12_out, and_15_out, and_16_out);
  and and_11 (and_11_out, in_1, in_4, in_7);
  and and_12 (and_12_out, in_18, in_15, in_12);
  and and_13 (and_13_out, in_1, in_5, in_9);
  and and_14 (and_14_out, in_3, in_5, in_7);
  and and_15 (and_15_out, in_18, in_14, in_10);
  and and_16 (and_16_out, in_16, in_14, in_12);
  or or_3 (out_19, out_20[1], out_21[1]);

  assign {out_20[2], out_20[0]} = {2{out_19}};
  assign {out_21[2], out_21[0]} = {2{out_20[1]}};
  assign out_22 = {out_19, out_20[1], out_19};
endmodule

module check (
  input  [2:0] in_1,
  output out_2,
  output out_3
);

  wire not_1_out;

  not not_1 (not_1_out, in_1[1]);
  and and_1 (out_2, in_1[0], not_1_out, in_1[2]);
  and and_2 (out_3, in_1[0], in_1[1], in_1[2]);
endmodule
